// Logisim project TN5.circ as structural Verilog
module Warmup (
  input  A,
  input  B,
  output f
);

  wire not_1_out;

  not not_1 (not_1_out, B);
  and and_1 (f, A, not_1_out);
endmodule

module TN1 (
  input  A,
  input  B,
  input  C,
  output Not,
  output AND,
  output OR,
  output NAND,
  output NOR,
  output XOR,
  output XNOR,
  output NAND3,
  output CHAIN,
  output XOR3
);

  not not_1 (Not, A);
  and and_1 (AND, A, B);
  or or_1 (OR, A, B);
  nand X (NAND, A, B);
  nor nor_1 (NOR, A, B);
  xor xor_1 (XOR, A, B);
  xnor xnor_1 (XNOR, A, B);
  nand nand_1 (NAND3, A, B, C);
  ExactlyOne xor_2 (.out(XOR3), .in0(A), .in1(B), .in2(C));
  nand Y (CHAIN, NAND, C);
endmodule

module TN2 (
  input  x,
  input  y,
  input  z,
  output EQ1,
  output EQ2,
  output EQ3,
  output EQ4,
  output EQ5
);

  wire L1_out, L2_out, L3_out, L4_out, not_1_out, not_2_out, R1_R2_out, R3_out, x_prime_y_out, x_y_out,
       x_z_out, y_z_out;

  not not_1 (not_1_out, x);
  not not_2 (not_2_out, y);
  and R1_R2 (R1_R2_out, not_1_out, not_2_out);
  and y_z (y_z_out, y, z);
  or x_z (x_z_out, x, z);
  and x_prime_y (x_prime_y_out, not_1_out, y);
  nor L1 (L1_out, x, y);
  not x_y (x_y_out, L1_out);
  nand L2 (L2_out, x, y);
  or L3 (L3_out, x, y_z_out);
  or L4 (L4_out, x, x_prime_y_out);
  and R3 (R3_out, x_y_out, x_z_out);
  xnor xnor_1 (EQ1, L1_out, R1_R2_out);
  xnor xnor_2 (EQ2, R1_R2_out, L2_out);
  xnor xnor_3 (EQ3, L3_out, R3_out);
  xnor xnor_4 (EQ4, L4_out, x);
  xnor xnor_5 (EQ5, L4_out, x_y_out);
endmodule

module TN3 (
  input  A,
  input  B,
  input  C,
  input  D,
  output F
);

  wire m2_out, m3_out, m5_out, m7_out, m11_out, m13_out, not_1_out, not_2_out, not_3_out, not_4_out;

  not not_1 (not_1_out, A);
  not not_2 (not_2_out, B);
  not not_3 (not_3_out, C);
  not not_4 (not_4_out, D);
  and m2 (m2_out, not_1_out, not_2_out, C, not_4_out);
  and m3 (m3_out, not_1_out, not_2_out, C, D);
  and m5 (m5_out, not_1_out, B, not_3_out, D);
  and m7 (m7_out, not_1_out, B, C, D);
  and m11 (m11_out, A, not_2_out, C, D);
  and m13 (m13_out, A, B, not_3_out, D);
  or or_1 (F, m2_out, m3_out, m5_out, m7_out, m11_out, m13_out);
endmodule

module TN4 (
  input  A,
  input  B,
  input  C,
  input  D,
  output EQ1,
  output EQ2
);

  wire A_prime_B_prime_C_out, A_prime_B_prime_C_prime_out, A_prime_BD_out, A_prime_D_out, B_C_out,
       B_prime_CD_out, B_prime_D_out, BC_prime_D_out, F_can_out, F_PoS_out, m2_out, m3_out, m5_out, m7_out,
       m11_out, m13_out, not_1_out, not_2_out, not_3_out, not_4_out, or_1_out;

  not not_1 (not_1_out, A);
  not not_2 (not_2_out, B);
  not not_3 (not_3_out, C);
  not not_4 (not_4_out, D);
  and m2 (m2_out, not_1_out, not_2_out, C, not_4_out);
  and m3 (m3_out, not_1_out, not_2_out, C, D);
  and m5 (m5_out, not_1_out, B, not_3_out, D);
  and m7 (m7_out, not_1_out, B, C, D);
  and m11 (m11_out, A, not_2_out, C, D);
  and m13 (m13_out, A, B, not_3_out, D);
  and A_prime_B_prime_C (A_prime_B_prime_C_out, not_1_out, not_2_out, C);
  and A_prime_BD (A_prime_BD_out, not_1_out, B, D);
  and BC_prime_D (BC_prime_D_out, B, not_3_out, D);
  and B_prime_CD (B_prime_CD_out, not_2_out, C, D);
  or B_C (B_C_out, B, C);
  or B_prime_D (B_prime_D_out, not_2_out, D);
  or A_prime_D (A_prime_D_out, not_1_out, D);
  or A_prime_B_prime_C_prime (A_prime_B_prime_C_prime_out, not_1_out, not_2_out, not_3_out);
  or F_can (F_can_out, m2_out, m3_out, m5_out, m7_out, m11_out, m13_out);
  or or_1 (or_1_out, A_prime_B_prime_C_out, A_prime_BD_out, BC_prime_D_out, B_prime_CD_out);
  and F_PoS (F_PoS_out, B_C_out, B_prime_D_out, A_prime_D_out, A_prime_B_prime_C_prime_out);
  xnor xnor_1 (EQ1, F_can_out, or_1_out);
  xnor xnor_2 (EQ2, F_can_out, F_PoS_out);
endmodule

module TN5 (
  input  A,
  input  B,
  input  C,
  output F
);

  wire xor_1_out;

  xor xor_1 (xor_1_out, A, B);
  xor xor_2 (F, xor_1_out, C);
endmodule
